# Fritzing sketch pcb (saved by Fritzing 0.9.3b)
circuit board: 8.46667cm x 5.64444cm
breadboards: 1

parts:
  IC1 = Voltage Regulator [package=to220-igo]
  IC2 = Voltage Regulator [package=to220-igo]
  J1 = Basic Servo
  WeMos_D1_Mini1 = WeMos D1 Mini
  J2 = Screw terminal - 2 pins [package=THT]

nets:
  GND: IC1.GND, IC2.GND, J2.pin1
  N1: IC1.IN, IC2.IN, J1.gnd, WeMos_D1_Mini1.G, J2.pin2
  N2: IC1.OUT, J1.vcc
  N3: IC2.OUT, WeMos_D1_Mini1.5V
  N4: J1.pulse, WeMos_D1_Mini1.D0
